# Fritzing sketch OnOffShutdown (saved by Fritzing 0.9.3b)
breadboards: 1

parts:
  S1 = Momentary Switch [package=ksa_sealed_tac_switch]
  R1 = Resistor [tolerance=±5% resistance=12k package="1206 [SMD]"]
  LED1 = smd LED [color="Red (633nm)" package="0805 [SMD]"]
  R2 = Resistor [tolerance=±5% resistance=1k package="1206 [SMD]"]
  R3 = Resistor [tolerance=±5% resistance=1.2k package="1206 [SMD]"]
  Raspberry_Pi1 = Raspberry Pi 2

nets:
  N1: S1.2, R1.Pin_0, R3.Pin_1
  N2: S1.4, Raspberry_Pi1.3v3
  N3: R1.Pin_1, R2.Pin_1, Raspberry_Pi1.GND
  N4: LED1.cathode, R2.Pin_0
  N5: LED1.anode, Raspberry_Pi1.GPIO14
  N6: R3.Pin_0, Raspberry_Pi1.GPIO4

notes:
  Long leg is cathode (+) and short is anode (-)
