# Fritzing sketch ShiftRegister_7Segment (saved by Fritzing 0.9.3b)
breadboards: 1

parts:
  U1 = 74HC595 [package="DIP16 [THT]"]
  LED1 = RGB LED (com. cathode, rbg) [package="5 mm [THT]"]
  R1 = Resistor [tolerance=±5% resistance=220 package="1206 [SMD]"]
  R2 = Resistor [tolerance=±5% resistance=220 package="1206 [SMD]"]
  R3 = Resistor [tolerance=±5% resistance=220 package="1206 [SMD]"]

nets:
  N1: U1.Q1, R1.Pin_1
  N2: U1.Q2, R2.Pin_1
  N3: U1.Q3, R3.Pin_1
  N4: U1.GND, LED1.red_anode
  N5: LED1.common_cathode, R1.Pin_0
  N6: LED1.blue_anode, R2.Pin_0
  N7: LED1.green_anode, R3.Pin_0
