# Fritzing sketch PiAlarm_Full (saved by Fritzing 0.9.3b)
breadboards: 1

parts:
  Raspberry_Pi1 = Raspberry Pi 2  # not connected
  Q4 = Basic FET P-Channel [package="TO220 [THT]"]
  JACK2 = 2.1mm_DC_Barrel_Jack
  RGB_Strip_LED3 = RGB Strip LED
  Q5 = Basic FET P-Channel [package="TO220 [THT]"]
  Q6 = Basic FET P-Channel [package="TO220 [THT]"]
  LCD1 = LCD screen  # not connected
  U2 = RELAY [package=relay-jzc]  # not connected
  U3 = Vibration Motor- ROB-08449 [package=vibe-motor-10mm]  # not connected
  D1 = Schottky Diode [part_number=1N5817 package="Melf DO-213 AB [SMD]"]  # not connected
  R1 = Resistor [tolerance=±5% resistance=500 package="1206 [SMD]"]
  R2 = Resistor [tolerance=±5% resistance=1k package="1206 [SMD]"]
  S3 = Momentary Switch [package=ksa_sealed_tac_switch]
  JP1 = USB_MICROB_PLUG [package=micro-b-ra-th]  # not connected
  X1 = USB Connectors [package=usb-minib-nostop]  # not connected

nets:
  N1: Q4.drain, RGB_Strip_LED3.connector15
  N2: Q4.source, JACK2.connector2, Q5.source, Q6.source, R1.Pin_0
  N3: JACK2.connector1, RGB_Strip_LED3.connector12
  N4: RGB_Strip_LED3.connector13, Q5.drain
  N5: RGB_Strip_LED3.connector14, Q6.drain
  N6: R1.Pin_1, S3.4
  N7: R2.Pin_1, S3.2

notes:
  ^ DC Barrel `side pin` alerts if something is plugged in or not
  Make Part: DROK DC-DC Buck Voltage Converter 4.5-40V 12V to 5V/2A Step-down Volt Transformer Stabilizer Voltage Regulator Module
