# Fritzing sketch RGB LED Strip (saved by Fritzing 0.9.3b)
breadboards: 1

parts:
  Q1 = Basic FET P-Channel [package="TO220 [THT]"]
  Q2 = Basic FET P-Channel [package="TO220 [THT]"]
  Q3 = Basic FET P-Channel [package="TO220 [THT]"]
  Raspberry_Pi1 = Raspberry Pi 2
  JACK1 = 2.1mm_DC_Barrel_Jack
  RGB_Strip_LED1 = RGB Strip LED

nets:
  N1: Q1.gate, Raspberry_Pi1.GPIO19
  N2: Q1.drain, RGB_Strip_LED1.connector15
  N3: Q1.source, Q2.source, Q3.source, Raspberry_Pi1.GND, JACK1.connector2
  N4: Q2.gate, Raspberry_Pi1.GPIO16
  N5: Q2.drain, RGB_Strip_LED1.connector14
  N6: Q3.gate, Raspberry_Pi1.GPIO20
  N7: Q3.drain, RGB_Strip_LED1.connector13
  N8: JACK1.connector1, RGB_Strip_LED1.connector12

notes:
  ^ DC Barrel `side pin` alerts if something is plugged in or not
