# Fritzing sketch Solder Sucker (saved by Fritzing 0.9.3b)
breadboards: 1

parts:
  Part1 = Arduino Uno (Rev3) - ICSP
  Q1 = Basic FET N-Channel [package="D2Pak [SMD]"]
  R1 = Resistor [tolerance=±5% resistance=10k package="1206 [SMD]"]
  JACK1 = 2.1mm_DC_Barrel_Jack
  F1 = fan_Ventilador
  POT1 = Breadboard_Trimpot

nets:
  N1: Part1.A0, POT1.connector2
  N2: Part1.D10_PWM/SS, Q1.Gate
  N3: Part1.GND, R1.Pin_1, JACK1.connector2, POT1.connector3
  N4: Part1.5V, POT1.connector1
  N5: Q1.drain, F1.connector1
  N6: Q1.source, R1.Pin_0
  N7: JACK1.connector1, F1.connector0

notes:
  12V ->
